# Fritzing sketch CRP_V3 (saved by Fritzing 0.9.4)
breadboards: 1

parts:
  Part4 = Arduino Uno (Rev3) - ICSP
  J2 = Basic Force Sensing Resistor (FSR) [package=THT]
  BAT3 = BC9VPC [package=bc9vpc]
  SP2 = SPEAKER [package=pcb_mount_speaker]
  DFRobot_DFPlayer_Mini2 = DFRobot DFPlayer Mini [part_number=DFR0299]
  R13 = Resistor [tolerance=±5% resistance=10k package=THT]
  R14 = Heating Pad
  U7 = Vibration Motor- ROB-08449 [package=vibe-motor-10mm]
  LED1 = prefix0000
  LED2 = prefix0000
  LED3 = prefix0000
  M1 = Dagu DGServo 9g (Top view) [part_number=RS001B]
  M2 = Dagu DGServo 9g (Top view) [part_number=RS001B]
  R15 = Resistor [tolerance=±5% resistance=10k package=THT]
  R16 = Resistor [tolerance=±5% resistance=330 package=THT]
  R17 = Resistor [tolerance=±5% resistance=330 package=THT]
  R18 = Resistor [tolerance=±5% resistance=330 package=THT]

nets:
  N1: Part4.A0, J2.pin_1, R15.Pin_0
  N2: Part4.D8, R13.Pin_1
  N3: Part4.D9_PWM, R17.Pin_1
  N4: Part4.D10_PWM/SS, R18.Pin_1
  N5: Part4.D2, U7.-
  N6: Part4.D3_PWM, M1.pulse
  N7: Part4.D5_PWM, R16.Pin_1
  N8: Part4.D7, DFRobot_DFPlayer_Mini2.TX
  N9: Part4.3V3, R14.pin_0
  VCC: Part4.5V, J2.pin_0, DFRobot_DFPlayer_Mini2.VCC, LED1.connector1, LED2.connector1, LED3.connector1, M2.vcc
  GND: Part4.GND, BAT3.V-, DFRobot_DFPlayer_Mini2.GND-1, DFRobot_DFPlayer_Mini2.GND-2, R14.pin_1, U7.+, LED1.connector3, LED2.connector3, LED3.connector3, M2.gnd, R15.Pin_1
  N10: Part4.VIN, BAT3.V+
  N11: SP2.+, DFRobot_DFPlayer_Mini2.SPK_2
  N12: SP2.-, DFRobot_DFPlayer_Mini2.SPK_1
  N13: DFRobot_DFPlayer_Mini2.RX, R13.Pin_0
  N14: LED2.connector2, R16.Pin_0
  N15: LED3.connector2, R17.Pin_0

custom parts:
  Heating Pad: A thermoresistant material with an embeded conductor that dissipates electrical energy into heat.
